# Fritzing sketch 20 (saved by Fritzing 0.9.1b)
breadboards: 1

parts:
  パーツ1 = Arduino Leonardo (Rev3b)
  J1 = Basic Force Sensing Resistor (FSR) [package=THT]
  R2 = Resistor [tolerance=±5% resistance=10k package=THT]

nets:
  N1: パーツ1.5V, R2.Pin_0
  N2: パーツ1.GND, J1.pin_0
  N3: パーツ1.A0, J1.pin_1, R2.Pin_1
